# Fritzing sketch HardwareDiagram (saved by Fritzing 0.9.2b)

parts:
  Part1 = SparkFun ESP8266 Thing [part_number=Arduino]
  R1 = Resistor [tolerance=±5% resistance=220k part_number=resistor package="0805 [SMD]"]
  BAT1 = LIPO-110mAh [part_number=Battery package=lipo-110]  # not connected

nets:
  N1: Part1.ADC, R1.Pin_0

notes:
  Normally closed circuit monitors for power loss, battery failure, or backup pump activation.
  Cheap commercial moisture sensor with still functional audio alarm tapped into to monitor for water too high up the pump basin.
  Rechargable 400mAh LiPo battery provides UPS during power loss.
